// Logisim project Encoder Decoder.circ as structural Verilog
module _2_4_Decoder_Active_high_output (
  input  wo,
  input  w1,
  input  ENABLE,
  output yo,
  output y1,
  output y2,
  output y3
);

  wire not_1_out, not_2_out;

  not not_1 (not_1_out, wo);
  not not_2 (not_2_out, w1);
  and and_1 (yo, not_1_out, not_2_out, ENABLE);
  and and_2 (y1, wo, not_2_out, ENABLE);
  and and_3 (y2, w1, not_1_out, ENABLE);
  and and_4 (y3, wo, w1, ENABLE);
endmodule

module _2_4_Decoder_Active_low_output (
  input  wo,
  input  w1,
  input  in_3,
  output yo,
  output y1,
  output y2,
  output y3
);

  wire not_1_out, not_2_out;

  not not_1 (not_1_out, wo);
  not not_2 (not_2_out, w1);
  nand nand_1 (yo, not_1_out, not_2_out, in_3);
  nand nand_2 (y1, wo, not_2_out, in_3);
  nand nand_3 (y2, w1, not_1_out, in_3);
  nand nand_4 (y3, wo, w1, in_3);
endmodule

module _3_8_decoder_modular (
  input  W0,
  input  W1,
  input  W2,
  output y0,
  output y1,
  output y2,
  output y4,
  output out_8,
  output y6,
  output y7,
  output y8
);

  wire not_1_out;

  not not_1 (not_1_out, W2);
  _2_4_Decoder_Active_high_output u_2_4_decoder_active_high_output_1 (
    .wo(W0), .w1(W1), .ENABLE(not_1_out), .yo(y0), .y1(y1), .y2(y2), .y3(y4));
  _2_4_Decoder_Active_high_output u_2_4_decoder_active_high_output_2 (
    .wo(W0), .w1(W1), .ENABLE(W2), .yo(out_8), .y1(y6), .y2(y7), .y3(y8));

  // Notes on the sheet:
  //   LSB
  //   MSB
endmodule

module Decoder_used_for_sum_and_c_out (
);


  // Notes on the sheet:
  //   All minterms are avialable to you
  //   for sum and Cout
  //   Avtive high NOR
  //   Active low AND
endmodule

module _3_8_decoder__Active_high__with_enable (
  input  EN,
  input  W0,
  input  W1,
  input  W2,
  output y0,
  output y1,
  output y2,
  output y3,
  output y4,
  output y5,
  output y6,
  output y7
);

  wire n2_4_decoder_active_high_output_1_y1, n2_4_decoder_active_high_output_1_y2,
       n2_4_decoder_active_high_output_1_y3, n2_4_decoder_active_high_output_1_yo,
       n2_4_decoder_active_high_output_2_y1, n2_4_decoder_active_high_output_2_y2,
       n2_4_decoder_active_high_output_2_y3, n2_4_decoder_active_high_output_2_yo, not_1_out;

  not not_1 (not_1_out, W2);
  _2_4_Decoder_Active_high_output u_2_4_decoder_active_high_output_1 (
    .wo(W0), .w1(W1), .ENABLE(not_1_out), .yo(n2_4_decoder_active_high_output_1_yo),
    .y1(n2_4_decoder_active_high_output_1_y1), .y2(n2_4_decoder_active_high_output_1_y2),
    .y3(n2_4_decoder_active_high_output_1_y3));
  _2_4_Decoder_Active_high_output u_2_4_decoder_active_high_output_2 (
    .wo(W0), .w1(W1), .ENABLE(W2), .yo(n2_4_decoder_active_high_output_2_yo),
    .y1(n2_4_decoder_active_high_output_2_y1), .y2(n2_4_decoder_active_high_output_2_y2),
    .y3(n2_4_decoder_active_high_output_2_y3));
  and and_1 (y0, EN, n2_4_decoder_active_high_output_1_yo);
  and and_2 (y1, EN, n2_4_decoder_active_high_output_1_y1);
  and and_3 (y2, EN, n2_4_decoder_active_high_output_1_y2);
  and and_4 (y3, EN, n2_4_decoder_active_high_output_1_y3);
  and and_5 (y4, EN, n2_4_decoder_active_high_output_2_yo);
  and and_6 (y5, EN, n2_4_decoder_active_high_output_2_y1);
  and and_7 (y6, EN, n2_4_decoder_active_high_output_2_y2);
  and and_8 (y7, n2_4_decoder_active_high_output_2_y3, EN);

  // Notes on the sheet:
  //   LSB
  //   MSB
  //   2-4 enable decoder
  //   2-4 enable decoder
  //   3-8 lin decoder with enable, if u dont want enable remove all the and gates lol
endmodule

module _8_3_Encoder (
  input  y7,
  input  y6,
  input  y5,
  input  y4,
  input  y3,
  input  y2,
  input  y1,
  input  y0,
  output A2,
  output A1,
  output A0
);

  or or_1 (A2, y7, y6, y5, y4);
  or or_2 (A1, y7, y6, y3, y2);
  or or_3 (A0, y7, y5, y3, y1);
endmodule

module Priority_Encoder (
  input  y3,
  input  y2,
  input  y1,
  input  y0,
  output o1,
  output o0,
  output v
);

  wire and_1_out, not_1_out;

  not not_1 (not_1_out, y2);
  or or_1 (o1, y3, y2);
  and and_1 (and_1_out, not_1_out, y1);
  or or_2 (o0, y3, and_1_out);
  or or_3 (v, o1, y1, y0);

  // Notes on the sheet:
  //   More than 1 I/P is high then the priority is given to the highest number
endmodule

module _4_1_Multiplexer (
  input  wo__select_lines,
  input  w1,
  input  I0,
  input  I1,
  input  I2,
  input  I3,
  input  ENABLE,
  output yo,
  output y1,
  output Output,
  output y2,
  output y3
);

  wire not_1_out, not_2_out;

  not not_1 (not_1_out, wo__select_lines);
  not not_2 (not_2_out, w1);
  and and_1 (yo, not_1_out, I0, not_2_out, ENABLE);
  and and_2 (y1, wo__select_lines, not_2_out, I1, ENABLE);
  and and_3 (y2, w1, I2, not_1_out, ENABLE);
  and and_4 (y3, I3, wo__select_lines, w1, ENABLE);
  or or_1 (Output, yo, y1, y2, y3);

  // Notes on the sheet:
  //   LSB
  //   Universal func generator
endmodule

module _8_1_mux (
  input  C__LSB,
  input  B,
  input  A__MSB,
  input  I0,
  input  I1,
  input  I2,
  input  I3,
  input  I4,
  input  I5,
  input  I6,
  input  I7,
  output Output
);

  wire n4_1_multiplexer_1_output, n4_1_multiplexer_2_output, not_1_out;

  not not_1 (not_1_out, A__MSB);
  _4_1_Multiplexer u_4_1_multiplexer_1 (
    .wo__select_lines(C__LSB), .w1(B), .I0(I0), .I1(I1), .I2(I2), .I3(I3), .ENABLE(not_1_out),
    .Output(n4_1_multiplexer_1_output));  // open: yo, y1, y2, y3
  _4_1_Multiplexer u_4_1_multiplexer_2 (
    .wo__select_lines(C__LSB), .w1(B), .I0(I4), .I1(I5), .I2(I6), .I3(I7), .ENABLE(A__MSB),
    .Output(n4_1_multiplexer_2_output));  // open: yo, y1, y2, y3
  or or_1 (Output, n4_1_multiplexer_1_output, n4_1_multiplexer_2_output);
endmodule

module _2_1_mux (
  input  S0,
  input  I0,
  input  I1,
  input  EN,
  output Output
);

  wire and_1_out, and_2_out, not_1_out;

  not not_1 (not_1_out, S0);
  and and_1 (and_1_out, S0, EN, I0);
  and and_2 (and_2_out, not_1_out, EN, I1);
  or or_1 (Output, and_1_out, and_2_out);

  // Notes on the sheet:
  //   S0'*I0+S0*I1
endmodule

module FASTER_8_1_MUX (
  input  A__MSB,
  input  B,
  input  C__LSB,
  input  I0,
  input  I1,
  input  I2,
  input  I3,
  input  I4,
  input  I5,
  input  I6,
  input  I7,
  input  En,
  output Output
);

  wire n4_1_multiplexer_1_output, n4_1_multiplexer_2_output;

  _4_1_Multiplexer u_4_1_multiplexer_1 (
    .wo__select_lines(C__LSB), .w1(B), .I0(I0), .I1(I1), .I2(I2), .I3(I3), .ENABLE(En),
    .Output(n4_1_multiplexer_1_output));  // open: yo, y1, y2, y3
  _4_1_Multiplexer u_4_1_multiplexer_2 (
    .wo__select_lines(C__LSB), .w1(B), .I0(I4), .I1(I5), .I2(I6), .I3(I7), .ENABLE(En),
    .Output(n4_1_multiplexer_2_output));  // open: yo, y1, y2, y3
  _2_1_mux u_2_1_mux_1 (
    .S0(A__MSB), .I0(n4_1_multiplexer_1_output), .I1(n4_1_multiplexer_2_output), .EN(En), .Output(Output));
endmodule

module _3_8_decode_without_enable (
  input  W0,
  input  W1,
  input  W2,
  output y0,
  output y1,
  output y2,
  output y3,
  output y4,
  output y5,
  output y6,
  output y7
);

  wire not_1_out;

  not not_1 (not_1_out, W2);
  _2_4_Decoder_Active_high_output u_2_4_decoder_active_high_output_1 (
    .wo(W0), .w1(W1), .ENABLE(not_1_out), .yo(y0), .y1(y1), .y2(y2), .y3(y3));
  _2_4_Decoder_Active_high_output u_2_4_decoder_active_high_output_2 (
    .wo(W0), .w1(W1), .ENABLE(W2), .yo(y4), .y1(y5), .y2(y6), .y3(y7));

  // Notes on the sheet:
  //   LSB
  //   MSB
  //   2-4 enable decoder
  //   2-4 enable decoder
endmodule

module _3_8_decoder_using_only_decoders (
  input  w0,
  input  w1,
  input  w2,
  input  EN,
  output y0,
  output y1,
  output y2,
  output y3,
  output y4,
  output y5,
  output y6,
  output y7
);

  wire n1_2_decoder_1_y0, n1_2_decoder_1_y1;

  _1_2_decoder u_1_2_decoder_1 (.S(w2), .EN(EN), .y0(n1_2_decoder_1_y0), .y1(n1_2_decoder_1_y1));
  _2_4_Decoder_Active_high_output u_2_4_decoder_active_high_output_1 (
    .wo(w0), .w1(w1), .ENABLE(n1_2_decoder_1_y0), .yo(y0), .y1(y1), .y2(y2), .y3(y3));
  _2_4_Decoder_Active_high_output u_2_4_decoder_active_high_output_2 (
    .wo(w0), .w1(w1), .ENABLE(n1_2_decoder_1_y1), .yo(y4), .y1(y5), .y2(y6), .y3(y7));

  // Notes on the sheet:
  //   LSB
  //   MSB
  //   2-4 enable decoder
  //   2-4 enable decoder
endmodule

module _1_2_decoder (
  input  S,
  input  EN,
  output y0,
  output y1
);

  wire not_1_out, not_2_out;

  not not_1 (not_1_out, S);
  not not_2 (not_2_out, not_1_out);
  and and_1 (y1, not_2_out, EN);
  and and_2 (y0, not_1_out, EN);
endmodule

module Full_ADDER_3_8_DECODER_ACTIVE_HIGH__MINTERMS (
  input  EN,
  input  Cin,
  input  B,
  input  A,
  output Sum,
  output Cout
);

  wire n3_8_decoder_active_high_with_enable_1_y1, n3_8_decoder_active_high_with_enable_1_y2,
       n3_8_decoder_active_high_with_enable_1_y3, n3_8_decoder_active_high_with_enable_1_y4,
       n3_8_decoder_active_high_with_enable_1_y5, n3_8_decoder_active_high_with_enable_1_y6,
       n3_8_decoder_active_high_with_enable_1_y7;

  _3_8_decoder__Active_high__with_enable u_3_8_decoder_active_high_with_enable_1 (
    .EN(EN), .W0(Cin), .W1(B), .W2(A), .y1(n3_8_decoder_active_high_with_enable_1_y1),
    .y2(n3_8_decoder_active_high_with_enable_1_y2), .y3(n3_8_decoder_active_high_with_enable_1_y3),
    .y4(n3_8_decoder_active_high_with_enable_1_y4), .y5(n3_8_decoder_active_high_with_enable_1_y5),
    .y6(n3_8_decoder_active_high_with_enable_1_y6), .y7(n3_8_decoder_active_high_with_enable_1_y7));  // open: y0
  or or_1 (Cout, n3_8_decoder_active_high_with_enable_1_y7, n3_8_decoder_active_high_with_enable_1_y6, n3_8_decoder_active_high_with_enable_1_y5, n3_8_decoder_active_high_with_enable_1_y3);
  or or_2 (Sum, n3_8_decoder_active_high_with_enable_1_y1, n3_8_decoder_active_high_with_enable_1_y2, n3_8_decoder_active_high_with_enable_1_y4, n3_8_decoder_active_high_with_enable_1_y7);

  // Notes on the sheet:
  //   MINTERMS
  //   Cout 3 5 6 7 
  //   Sum 1 2 4 7
  //   FOR ACTIVE LOW OUTPUT  CONNECT NAND GATE INSTEAD OF OR GATE
endmodule

module FULL_ADDER_3_8_DECODER_active_high_MAXTERMS (
  input  EN,
  input  in_2,
  input  in_3,
  input  in_4,
  output Sum,
  output Cout
);

  wire n3_8_decoder_active_high_with_enable_1_y0, n3_8_decoder_active_high_with_enable_1_y1,
       n3_8_decoder_active_high_with_enable_1_y2, n3_8_decoder_active_high_with_enable_1_y3,
       n3_8_decoder_active_high_with_enable_1_y4, n3_8_decoder_active_high_with_enable_1_y5,
       n3_8_decoder_active_high_with_enable_1_y6;

  _3_8_decoder__Active_high__with_enable u_3_8_decoder_active_high_with_enable_1 (
    .EN(EN), .W0(in_2), .W1(in_3), .W2(in_4), .y0(n3_8_decoder_active_high_with_enable_1_y0),
    .y1(n3_8_decoder_active_high_with_enable_1_y1), .y2(n3_8_decoder_active_high_with_enable_1_y2),
    .y3(n3_8_decoder_active_high_with_enable_1_y3), .y4(n3_8_decoder_active_high_with_enable_1_y4),
    .y5(n3_8_decoder_active_high_with_enable_1_y5), .y6(n3_8_decoder_active_high_with_enable_1_y6));  // open: y7
  nor nor_1 (Cout, n3_8_decoder_active_high_with_enable_1_y4, n3_8_decoder_active_high_with_enable_1_y2, n3_8_decoder_active_high_with_enable_1_y1, n3_8_decoder_active_high_with_enable_1_y0);
  nor nor_2 (Sum, n3_8_decoder_active_high_with_enable_1_y0, n3_8_decoder_active_high_with_enable_1_y3, n3_8_decoder_active_high_with_enable_1_y5, n3_8_decoder_active_high_with_enable_1_y6);

  // Notes on the sheet:
  //   MAXTERMS
  //   FOR ACTIVE LOW PINS USE AND GATE
  //   Sum Max 0 3 5 6
  //   C out Max 0 1 2 4
endmodule

module _4_3_encoder (
  input  A0,
  input  A1,
  input  A2,
  input  A3,
  output o0,
  output o1,
  output d___discriminant
);

  or or_1 (o0, A3, A1);
  or or_2 (o1, A2, A3);
  or or_3 (d___discriminant, A0, A1, A2, A3);

  // Notes on the sheet:
  //   To add enable just and these with an and gate
endmodule

module _3_8_Decoder_Active_low_outputs (
  input  EN,
  input  W0,
  input  W1,
  input  W2,
  output y0,
  output y1,
  output y2,
  output y3,
  output y4,
  output y5,
  output y6,
  output y7
);

  wire and_1_out, and_2_out, and_3_out, and_4_out, and_5_out, and_6_out, and_7_out, and_8_out,
       n2_4_decoder_active_high_output_1_y1, n2_4_decoder_active_high_output_1_y2,
       n2_4_decoder_active_high_output_1_y3, n2_4_decoder_active_high_output_1_yo,
       n2_4_decoder_active_high_output_2_y1, n2_4_decoder_active_high_output_2_y2,
       n2_4_decoder_active_high_output_2_y3, n2_4_decoder_active_high_output_2_yo, not_1_out;

  not not_1 (not_1_out, W2);
  _2_4_Decoder_Active_high_output u_2_4_decoder_active_high_output_1 (
    .wo(W0), .w1(W1), .ENABLE(not_1_out), .yo(n2_4_decoder_active_high_output_1_yo),
    .y1(n2_4_decoder_active_high_output_1_y1), .y2(n2_4_decoder_active_high_output_1_y2),
    .y3(n2_4_decoder_active_high_output_1_y3));
  _2_4_Decoder_Active_high_output u_2_4_decoder_active_high_output_2 (
    .wo(W0), .w1(W1), .ENABLE(W2), .yo(n2_4_decoder_active_high_output_2_yo),
    .y1(n2_4_decoder_active_high_output_2_y1), .y2(n2_4_decoder_active_high_output_2_y2),
    .y3(n2_4_decoder_active_high_output_2_y3));
  and and_1 (and_1_out, EN, n2_4_decoder_active_high_output_1_yo);
  not not_2 (y0, and_1_out);
  not not_3 (y1, and_2_out);
  and and_2 (and_2_out, EN, n2_4_decoder_active_high_output_1_y1);
  and and_3 (and_3_out, EN, n2_4_decoder_active_high_output_1_y2);
  not not_4 (y2, and_3_out);
  and and_4 (and_4_out, EN, n2_4_decoder_active_high_output_1_y3);
  not not_5 (y3, and_4_out);
  and and_5 (and_5_out, EN, n2_4_decoder_active_high_output_2_yo);
  not not_6 (y4, and_5_out);
  not not_7 (y5, and_6_out);
  and and_6 (and_6_out, EN, n2_4_decoder_active_high_output_2_y1);
  and and_7 (and_7_out, EN, n2_4_decoder_active_high_output_2_y2);
  not not_8 (y6, and_7_out);
  and and_8 (and_8_out, n2_4_decoder_active_high_output_2_y3, EN);
  not not_9 (y7, and_8_out);

  // Notes on the sheet:
  //   LSB
  //   MSB
  //   2-4 enable decoder
  //   2-4 enable decoder
endmodule

module _4_16_decoder (
  input  A0,
  input  A1,
  input  A2,
  input  A3,
  input  EN,
  output D0,
  output out_7,
  output out_8,
  output out_9,
  output out_10,
  output out_11,
  output out_12,
  output out_13,
  output out_14,
  output out_15,
  output out_16,
  output out_17,
  output out_18,
  output out_19,
  output out_20,
  output out_21
);

  wire n2_4_decoder_active_high_output_1_y1, n2_4_decoder_active_high_output_1_y2,
       n2_4_decoder_active_high_output_1_y3, n2_4_decoder_active_high_output_1_yo;

  _2_4_Decoder_Active_high_output u_2_4_decoder_active_high_output_1 (
    .wo(A2), .w1(A3), .ENABLE(EN), .yo(n2_4_decoder_active_high_output_1_yo),
    .y1(n2_4_decoder_active_high_output_1_y1), .y2(n2_4_decoder_active_high_output_1_y2),
    .y3(n2_4_decoder_active_high_output_1_y3));
  _2_4_Decoder_Active_high_output u_2_4_decoder_active_high_output_2 (
    .wo(A0), .w1(A0), .ENABLE(n2_4_decoder_active_high_output_1_yo), .yo(D0), .y1(out_7), .y2(out_8),
    .y3(out_9));
  _2_4_Decoder_Active_high_output u_2_4_decoder_active_high_output_3 (
    .wo(A0), .w1(A0), .ENABLE(n2_4_decoder_active_high_output_1_y1), .yo(out_10), .y1(out_11), .y2(out_12),
    .y3(out_13));
  _2_4_Decoder_Active_high_output u_2_4_decoder_active_high_output_4 (
    .wo(A0), .w1(A0), .ENABLE(n2_4_decoder_active_high_output_1_y2), .yo(out_14), .y1(out_15), .y2(out_16),
    .y3(out_17));
  _2_4_Decoder_Active_high_output u_2_4_decoder_active_high_output_5 (
    .wo(A0), .w1(A0), .ENABLE(n2_4_decoder_active_high_output_1_y3), .yo(out_18), .y1(out_19), .y2(out_20),
    .y3(out_21));

  assign A1 = A0;
endmodule
