// Logisim project Lab 4.circ as structural Verilog: 5 circuits, main circuit main
module main (
  input  wo,
  input  w1,
  input  in_3,
  output yo,
  output y1,
  output y2,
  output y3
);

  wire not_1_out, not_2_out;

  not not_1 (not_1_out, wo);
  not not_2 (not_2_out, w1);
  nand nand_1 (yo, not_1_out, not_2_out, in_3);
  nand nand_2 (y1, wo, not_2_out, in_3);
  nand nand_3 (y2, w1, not_1_out, in_3);
  nand nand_4 (y3, wo, w1, in_3);
endmodule

module _2_4_Decoder_Active_low_output (
  input  wo,
  input  w1,
  input  ENABLE,
  output yo,
  output y1,
  output y2,
  output y3
);

  wire not_1_out, not_2_out;

  not not_1 (not_1_out, wo);
  not not_2 (not_2_out, w1);
  nand nand_1 (yo, not_1_out, not_2_out, ENABLE);
  nand nand_2 (y1, wo, not_2_out, ENABLE);
  nand nand_3 (y2, w1, not_1_out, ENABLE);
  nand nand_4 (y3, wo, w1, ENABLE);
endmodule

module _1_2_Decoder_Active_Low_Output (
  input  S,
  input  EN,
  output y0,
  output y1
);

  wire not_1_out, not_2_out;

  not not_1 (not_1_out, S);
  not not_2 (not_2_out, not_1_out);
  nand nand_1 (y1, not_2_out, EN);
  nand nand_2 (y0, not_1_out, EN);
endmodule

module _3_8_Decoder_Active_Low_Output (
  input  EN,
  input  W0,
  input  W1,
  input  W2,
  output y0,
  output y1,
  output y2,
  output y3,
  output y4,
  output y5,
  output y6,
  output y7
);

  wire n2_4_decoder_active_low_output_1_y1, n2_4_decoder_active_low_output_1_y2,
       n2_4_decoder_active_low_output_1_y3, n2_4_decoder_active_low_output_1_yo,
       n2_4_decoder_active_low_output_2_y1, n2_4_decoder_active_low_output_2_y2,
       n2_4_decoder_active_low_output_2_y3, n2_4_decoder_active_low_output_2_yo, not_1_out;

  not not_1 (not_1_out, W2);
  _2_4_Decoder_Active_low_output u_2_4_decoder_active_low_output_1 (
    .wo(W0), .w1(W1), .ENABLE(not_1_out), .yo(n2_4_decoder_active_low_output_1_yo),
    .y1(n2_4_decoder_active_low_output_1_y1), .y2(n2_4_decoder_active_low_output_1_y2),
    .y3(n2_4_decoder_active_low_output_1_y3));
  _2_4_Decoder_Active_low_output u_2_4_decoder_active_low_output_2 (
    .wo(W0), .w1(W1), .ENABLE(W2), .yo(n2_4_decoder_active_low_output_2_yo),
    .y1(n2_4_decoder_active_low_output_2_y1), .y2(n2_4_decoder_active_low_output_2_y2),
    .y3(n2_4_decoder_active_low_output_2_y3));
  and and_1 (y0, EN, n2_4_decoder_active_low_output_1_yo);
  and and_2 (y1, EN, n2_4_decoder_active_low_output_1_y1);
  and and_3 (y2, EN, n2_4_decoder_active_low_output_1_y2);
  and and_4 (y3, EN, n2_4_decoder_active_low_output_1_y3);
  and and_5 (y4, EN, n2_4_decoder_active_low_output_2_yo);
  and and_6 (y5, EN, n2_4_decoder_active_low_output_2_y1);
  and and_7 (y6, EN, n2_4_decoder_active_low_output_2_y2);
  and and_8 (y7, n2_4_decoder_active_low_output_2_y3, EN);

  // Notes on the sheet:
  //   LSB
  //   MSB
  //   2-4 enable decoder
  //   2-4 enable decoder
endmodule

module _4_16_Line_Decoder (
  input  W0,
  input  W1,
  input  W2,
  input  W3,
  input  in_5,
  output y0,
  output y1,
  output y2,
  output y3,
  output y4,
  output y5,
  output y6,
  output y7,
  output y8,
  output y9,
  output y10,
  output y11,
  output y12,
  output y13,
  output y14,
  output y15
);

  wire n1_2_decoder_active_low_output_1_y0, n1_2_decoder_active_low_output_1_y1;

  _1_2_Decoder_Active_Low_Output u_1_2_decoder_active_low_output_1 (
    .S(W3), .EN(in_5), .y0(n1_2_decoder_active_low_output_1_y0), .y1(n1_2_decoder_active_low_output_1_y1));
  _3_8_Decoder_Active_Low_Output u_3_8_decoder_active_low_output_1 (
    .EN(n1_2_decoder_active_low_output_1_y0), .W0(W0), .W1(W1), .W2(W2), .y0(y0), .y1(y1), .y2(y2), .y3(y3),
    .y4(y4), .y5(y5), .y6(y6), .y7(y7));
  _3_8_Decoder_Active_Low_Output u_3_8_decoder_active_low_output_2 (
    .EN(n1_2_decoder_active_low_output_1_y1), .W0(W0), .W1(W1), .W2(W2), .y0(y8), .y1(y9), .y2(y10),
    .y3(y11), .y4(y12), .y5(y13), .y6(y14), .y7(y15));
endmodule
