// Logisim project Multiplexer Demultiplexer.circ as structural Verilog
module _4_1_Multiplexer (
  input  wo__select_lines,
  input  w1,
  input  I0,
  input  I1,
  input  I2,
  input  I3,
  input  ENABLE,
  output yo,
  output y1,
  output Output,
  output y2,
  output y3
);

  wire not_1_out, not_2_out;

  not not_1 (not_1_out, wo__select_lines);
  not not_2 (not_2_out, w1);
  and and_1 (yo, not_1_out, I0, not_2_out, ENABLE);
  and and_2 (y1, wo__select_lines, not_2_out, I1, ENABLE);
  and and_3 (y2, w1, I2, not_1_out, ENABLE);
  and and_4 (y3, I3, wo__select_lines, w1, ENABLE);
  or or_1 (Output, yo, y1, y2, y3);

  // Notes on the sheet:
  //   LSB
  //   Universal func generator
endmodule

module _2_1_mux (
  input  S0,
  input  I0,
  input  I1,
  input  EN,
  output Output
);

  wire and_1_out, and_2_out, not_1_out;

  not not_1 (not_1_out, S0);
  and and_1 (and_1_out, S0, EN, I0);
  and and_2 (and_2_out, not_1_out, EN, I1);
  or or_1 (Output, and_1_out, and_2_out);

  // Notes on the sheet:
  //   S0'*I0+S0*I1
endmodule

module _8_1_mux (
  input  C__LSB,
  input  B,
  input  A__MSB,
  input  I0,
  input  I1,
  input  I2,
  input  I3,
  input  I4,
  input  I5,
  input  I6,
  input  I7,
  output Output
);

  wire n4_1_multiplexer_1_output, n4_1_multiplexer_2_output, not_1_out;

  not not_1 (not_1_out, A__MSB);
  _4_1_Multiplexer u_4_1_multiplexer_1 (
    .wo__select_lines(C__LSB), .w1(B), .I0(I0), .I1(I1), .I2(I2), .I3(I3), .ENABLE(not_1_out),
    .Output(n4_1_multiplexer_1_output));  // open: yo, y1, y2, y3
  _4_1_Multiplexer u_4_1_multiplexer_2 (
    .wo__select_lines(C__LSB), .w1(B), .I0(I4), .I1(I5), .I2(I6), .I3(I7), .ENABLE(A__MSB),
    .Output(n4_1_multiplexer_2_output));  // open: yo, y1, y2, y3
  or or_1 (Output, n4_1_multiplexer_1_output, n4_1_multiplexer_2_output);
endmodule

module FASTER_8_1_MUX (
  input  A__MSB,
  input  B,
  input  C__LSB,
  input  I0,
  input  I1,
  input  I2,
  input  I3,
  input  I4,
  input  I5,
  input  I6,
  input  I7,
  input  En,
  output Output
);

  wire n4_1_multiplexer_1_output, n4_1_multiplexer_2_output;

  _4_1_Multiplexer u_4_1_multiplexer_1 (
    .wo__select_lines(C__LSB), .w1(B), .I0(I0), .I1(I1), .I2(I2), .I3(I3), .ENABLE(En),
    .Output(n4_1_multiplexer_1_output));  // open: yo, y1, y2, y3
  _4_1_Multiplexer u_4_1_multiplexer_2 (
    .wo__select_lines(C__LSB), .w1(B), .I0(I4), .I1(I5), .I2(I6), .I3(I7), .ENABLE(En),
    .Output(n4_1_multiplexer_2_output));  // open: yo, y1, y2, y3
  _2_1_mux u_2_1_mux_1 (
    .S0(A__MSB), .I0(n4_1_multiplexer_1_output), .I1(n4_1_multiplexer_2_output), .EN(En), .Output(Output));
endmodule

module Multiplexer_to_Demultiplexer (
  input  En,
  input  d1,
  input  d0,
  input  S0,
  input  in_5,
  input  in_6,
  input  in_7,
  input  in_8,
  input  in_9,
  input  En_2,
  output Y0,
  output Y1,
  output Y2,
  output Y3
);

  wire n4_1_multiplexer_1_output, not_1_out, not_2_out;

  _4_1_Multiplexer u_4_1_multiplexer_1 (
    .wo__select_lines(S0), .w1(in_5), .I0(in_6), .I1(in_7), .I2(in_8), .I3(in_9), .ENABLE(En_2),
    .Output(n4_1_multiplexer_1_output));  // open: yo, y1, y2, y3
  not not_1 (not_1_out, d1);
  not not_2 (not_2_out, d0);
  and and_1 (Y0, not_2_out, not_1_out, n4_1_multiplexer_1_output, En);
  and and_2 (Y1, not_1_out, d0, n4_1_multiplexer_1_output, En);
  and and_3 (Y2, not_2_out, d1, n4_1_multiplexer_1_output, En);
  and and_4 (Y3, d1, d0, n4_1_multiplexer_1_output, En);
endmodule

module Demultiplexer (
  input  En,
  input  d1,
  input  d0,
  input  DATA,
  output Y0,
  output Y1,
  output Y2,
  output Y3
);

  wire not_1_out, not_2_out;

  not not_1 (not_1_out, d1);
  not not_2 (not_2_out, d0);
  and and_1 (Y0, not_2_out, not_1_out, DATA, En);
  and and_2 (Y1, not_1_out, d0, DATA, En);
  and and_3 (Y2, not_2_out, d1, DATA, En);
  and and_4 (Y3, d1, d0, DATA, En);
endmodule
