// Logisim project lathches and Flip Flops.circ as structural Verilog
module Flip_FLOP (
  input  SET,
  input  ENABLE,
  input  RESET,
  output out_4,
  output out_5
);

  wire nand_1_out, nand_2_out;

  nand nand_1 (nand_1_out, SET, ENABLE);
  nand nand_2 (nand_2_out, ENABLE, RESET);
  nand nand_3 (out_4, nand_1_out, out_5);
  nand nand_4 (out_5, nand_2_out, out_4);
endmodule

module LATCH (
  input  in_1,
  input  in_2,
  output out_3,
  output out_4
);

  nand nand_1 (out_3, in_1, out_4);
  nand nand_2 (out_4, in_2, out_3);
endmodule

module J_K_Flip_Flop (
  input  SET,
  input  ENABLE,
  input  RESET,
  output out_4,
  output out_5
);

  wire nand_1_out, nand_2_out;

  nand nand_1 (nand_1_out, SET, out_5, ENABLE);
  nand nand_2 (nand_2_out, ENABLE, out_4, RESET);
  nand nand_3 (out_4, nand_1_out, out_5);
  nand nand_4 (out_5, nand_2_out, out_4, out_4);
endmodule

module Toggle_Flip_Flop (
  input  TOGGLE,
  input  ENABLE,
  output out_3,
  output out_4
);

  wire nand_1_out, nand_2_out;

  nand nand_1 (nand_1_out, TOGGLE, out_4, ENABLE);
  nand nand_2 (nand_2_out, ENABLE, out_3, TOGGLE);
  nand nand_3 (out_3, nand_1_out, out_4);
  nand nand_4 (out_4, nand_2_out, out_3, out_3);
endmodule

module Delay_Flip_Flop (
  input  DELAY,
  input  ENABLE,
  output out_3,
  output out_4
);

  wire nand_1_out, nand_2_out, not_1_out;

  not not_1 (not_1_out, DELAY);
  nand nand_1 (nand_1_out, DELAY, out_4, ENABLE);
  nand nand_2 (nand_2_out, ENABLE, out_3, not_1_out);
  nand nand_3 (out_3, nand_1_out, out_4);
  nand nand_4 (out_4, nand_2_out, out_3, out_3);
endmodule
